// Logisim project cpu-circuit.circ as structural Verilog: 1 circuit, main circuit main
module main (
  input  in_1,
  input  in_2
);

  wire adder_1_cout, and_1_out, and_2_out, and_3_out, and_4_out, and_6_out, and_7_out, and_8_out, CARR_BIT,
       CARRY_FLAG, CLK, clock_1_out, controlled_buffer_15_out, controlled_buffer_16_out, COUNT_ENABLE,
       counter_2_carry, d_ff_1_q, DISP_REG_WRITE, DIV, EI, EO, EXP_READ, EXP_WRITE, FLAG_REG_WRITE, INV_CLK,
       JUMP, LOAD_ROM, MEM_READ, MEM_WRITE, MULT, n7_segment_display_1_p1, n7_segment_display_2_p1,
       n7_segment_display_3_p1, n7_segment_display_4_p1, n7_segment_display_5_p1, n7_segment_display_6_p1,
       n7_segment_display_7_p1, n7_segment_display_8_p1, n7_segment_display_9_p1, n7_segment_display_10_p1,
       n7_segment_display_11_p1, n7_segment_display_12_p1, not_1_out, not_3_out, not_4_out, not_5_out,
       not_6_out, not_7_out, not_8_out, not_10_out, not_11_out, or_1_out, PRG_CNT_READ, REG_A_READ,
       REG_A_WRITE, REG_B_READ, REG_B_WRITE, REG_C_READ, REG_C_WRITE, REG_INS_READ, REG_INS_WRITE,
       REG_MEMADDR_WRITE, ROM_LOAD_CLOCK, STOP, SUB, ZERO_FLAG;
  wire [1:0] controlled_buffer_19_out;
  wire [3:0] buffer_10_out, controlled_buffer_18_out, controlled_buffer_20_out, INS_DECODER,
       INSTR_STEP_COUNTER_q;
  wire [5:0] rgb_video_1_p3, rgb_video_1_p4;
  wire [7:0] and_5_out, binary_to_bcd_converter_2_p1, buffer_2_out, counter_1_q;
  wire [7:2] register_1_q;
  wire [8:0] rom_1_data;
  wire [9:0] dipswitch_2_sw10;
  wire [11:0] controlled_buffer_13_out, counter_4_q, INSTR_REG_q;
  wire [15:0] adder_1_out, ALU_IN_A, ALU_IN_B, ALU_VALUE, buffer_3_out, controlled_buffer_22_out,
       controlled_inverter_1_out, dipswitch_1_sw16, DISP_REG_q, MEM_ADDRESS_REG_q, MEMORY_dout,
       multiplier_1_cout, multiplier_1_out, PROGRAM_ROM_data;

  Clock clock_1 (.out(clock_1_out));
  and and_1 (and_1_out, not_1_out, not_3_out);
  not not_1 (not_1_out, STOP);
  assign ROM_LOAD_CLOCK = LOAD_ROM ? clock_1_out : 1'bz;  // Controlled_Buffer controlled_buffer_1
  assign CLK = LOAD_ROM ? in_1 : 1'bz;  // Controlled_Buffer controlled_buffer_2
  assign CLK = and_1_out ? clock_1_out : 1'bz;  // Controlled_Buffer controlled_buffer_3
  not not_2 (INV_CLK, CLK);
  not not_3 (not_3_out, LOAD_ROM);
  // _7_Segment_Display 7_segment_display_1: pin names not known; wires that end beside it: n7_segment_display_1_p1, n7_segment_display_1_p1
  // BCD_to_7_Segment_decoder bcd_to_7_segment_decoder_1: pin names not known
  // Binary_to_BCD_converter #(.binvalue(8)) binary_to_bcd_converter_1: pin names not known
  // _7_Segment_Display 7_segment_display_2: pin names not known; wires that end beside it: n7_segment_display_2_p1, n7_segment_display_2_p1
  // BCD_to_7_Segment_decoder bcd_to_7_segment_decoder_2: pin names not known
  // _7_Segment_Display 7_segment_display_3: pin names not known; wires that end beside it: n7_segment_display_3_p1, n7_segment_display_3_p1
  // BCD_to_7_Segment_decoder bcd_to_7_segment_decoder_3: pin names not known
  // Buffer buffer_1 is placed but not wired
  LED led_1 (.in(binary_to_bcd_converter_2_p1[7]));
  LED led_2 (.in(binary_to_bcd_converter_2_p1[6]));
  LED led_3 (.in(binary_to_bcd_converter_2_p1[5]));
  LED led_4 (.in(binary_to_bcd_converter_2_p1[4]));
  // _7_Segment_Display 7_segment_display_4: pin names not known; wires that end beside it: n7_segment_display_4_p1, n7_segment_display_4_p1
  // _7_Segment_Display 7_segment_display_5: pin names not known; wires that end beside it: n7_segment_display_5_p1, n7_segment_display_5_p1
  // BCD_to_7_Segment_decoder bcd_to_7_segment_decoder_4: pin names not known
  // BCD_to_7_Segment_decoder bcd_to_7_segment_decoder_5: pin names not known
  // Binary_to_BCD_converter #(.binvalue(8)) binary_to_bcd_converter_2: pin names not known; wires that end beside it: binary_to_bcd_converter_2_p1
  LED led_5 (.in(binary_to_bcd_converter_2_p1[3]));
  LED led_6 (.in(binary_to_bcd_converter_2_p1[2]));
  LED led_7 (.in(binary_to_bcd_converter_2_p1[1]));
  LED led_8 (.in(binary_to_bcd_converter_2_p1[0]));
  // _7_Segment_Display 7_segment_display_6: pin names not known; wires that end beside it: n7_segment_display_6_p1, n7_segment_display_6_p1
  // BCD_to_7_Segment_decoder bcd_to_7_segment_decoder_6: pin names not known
  DipSwitch #(.number(16)) dipswitch_1 (
    .sw1(dipswitch_1_sw16[15]), .sw2(dipswitch_1_sw16[14]), .sw3(dipswitch_1_sw16[13]),
    .sw4(dipswitch_1_sw16[12]), .sw5(dipswitch_1_sw16[11]), .sw6(dipswitch_1_sw16[10]),
    .sw7(dipswitch_1_sw16[9]), .sw8(dipswitch_1_sw16[8]), .sw9(dipswitch_1_sw16[7]),
    .sw10(dipswitch_1_sw16[6]), .sw11(dipswitch_1_sw16[5]), .sw12(dipswitch_1_sw16[4]),
    .sw13(dipswitch_1_sw16[3]), .sw14(dipswitch_1_sw16[2]), .sw15(dipswitch_1_sw16[1]),
    .sw16(dipswitch_1_sw16[0]));
  // Probe on dipswitch_1_sw16
  // _7_Segment_Display 7_segment_display_7: pin names not known; wires that end beside it: n7_segment_display_7_p1, n7_segment_display_7_p1
  // BCD_to_7_Segment_decoder bcd_to_7_segment_decoder_7: pin names not known
  // Binary_to_BCD_converter #(.binvalue(8)) binary_to_bcd_converter_3: pin names not known; wires that end beside it: dipswitch_1_sw16[15:8]
  Register #(.width(16)) A_Reg (.D(ALU_VALUE), .en(REG_A_WRITE), .clk(CLK), .Q(ALU_IN_A));  // open: clr
  // _7_Segment_Display 7_segment_display_8: pin names not known; wires that end beside it: n7_segment_display_8_p1, n7_segment_display_8_p1
  // _7_Segment_Display 7_segment_display_9: pin names not known; wires that end beside it: n7_segment_display_9_p1, n7_segment_display_9_p1
  // BCD_to_7_Segment_decoder bcd_to_7_segment_decoder_8: pin names not known
  // BCD_to_7_Segment_decoder bcd_to_7_segment_decoder_9: pin names not known
  not not_4 (not_4_out, REG_A_WRITE);
  and and_2 (and_2_out, not_4_out, REG_A_READ);
  assign ALU_VALUE = and_2_out ? ALU_IN_A : 16'bz;  // Controlled_Buffer controlled_buffer_4
  // Probe on ALU_IN_A
  // _7_Segment_Display 7_segment_display_10: pin names not known; wires that end beside it: n7_segment_display_10_p1, n7_segment_display_10_p1
  // BCD_to_7_Segment_decoder bcd_to_7_segment_decoder_10: pin names not known
  // Binary_to_BCD_converter #(.binvalue(8)) binary_to_bcd_converter_4: pin names not known; wires that end beside it: dipswitch_1_sw16[7:0]
  not not_5 (not_5_out, SUB);
  // _7_Segment_Display 7_segment_display_11: pin names not known; wires that end beside it: n7_segment_display_11_p1, n7_segment_display_11_p1
  // BCD_to_7_Segment_decoder bcd_to_7_segment_decoder_11: pin names not known
  assign controlled_inverter_1_out = SUB ? ~ALU_IN_B : 16'bz;  // Controlled_Inverter controlled_inverter_1
  assign controlled_inverter_1_out = not_5_out ? ALU_IN_B : 16'bz;  // Controlled_Buffer controlled_buffer_5
  Counter counter_1 (
    .load(JUMP), .count(COUNT_ENABLE), .clk(CLK), .D(ALU_VALUE[7:0]), .Q(counter_1_q));  // open: clr, up, carry
  // _7_Segment_Display 7_segment_display_12: pin names not known; wires that end beside it: n7_segment_display_12_p1, n7_segment_display_12_p1
  // BCD_to_7_Segment_decoder bcd_to_7_segment_decoder_12: pin names not known
  Adder #(.width(16)) adder_1 (
    .a(controlled_inverter_1_out), .b(ALU_IN_A), .out(adder_1_out), .cin(SUB), .cout(adder_1_cout));
  assign CARR_BIT = and_3_out ? adder_1_cout : 1'bz;  // Controlled_Buffer controlled_buffer_6
  Multiplier #(.width(16)) multiplier_1 (
    .a(ALU_IN_B), .b(ALU_IN_A), .out(multiplier_1_out), .cout(multiplier_1_cout));  // open: cin
  or or_1 (or_1_out, multiplier_1_cout[15], multiplier_1_cout[14], multiplier_1_cout[13], multiplier_1_cout[12], multiplier_1_cout[11], multiplier_1_cout[10], multiplier_1_cout[9], multiplier_1_cout[8], multiplier_1_cout[7], multiplier_1_cout[6], multiplier_1_cout[5], multiplier_1_cout[4], multiplier_1_cout[3], multiplier_1_cout[2], multiplier_1_cout[1], multiplier_1_cout[0]);
  assign CARR_BIT = and_4_out ? or_1_out : 1'bz;  // Controlled_Buffer controlled_buffer_7
  and and_3 (and_3_out, ~MULT, EO);  // AND_Gate
  assign ALU_VALUE = and_3_out ? adder_1_out : 16'bz;  // Controlled_Buffer controlled_buffer_8
  and and_4 (and_4_out, MULT, EO);
  assign ALU_VALUE = and_4_out ? multiplier_1_out : 16'bz;  // Controlled_Buffer controlled_buffer_9
  // Probe on ALU_VALUE
  Register #(.width(16)) DISP_REG (.D(ALU_VALUE), .en(DISP_REG_WRITE), .clk(CLK), .Q(DISP_REG_q));  // open: clr
  Register #(.width(16)) B_REG (.D(ALU_VALUE), .en(REG_B_WRITE), .clk(CLK), .Q(ALU_IN_B));  // open: clr
  assign buffer_2_out = {8{1'b0}};  // Buffer buffer_2, 8 bits wide
  assign ALU_VALUE = PRG_CNT_READ ? {buffer_2_out, counter_1_q} : 16'bz;  // Controlled_Buffer controlled_buffer_10
  // Probe on DISP_REG_q
  // Probe on DISP_REG_q
  not not_6 (not_6_out, REG_B_WRITE);
  Controlled_Buffer #(.width(8)) controlled_buffer_11 (.en(not_6_out));  // open: in, out
  // Probe on ALU_IN_B
  // Probe on ALU_VALUE
  // RGB_Video #(.height(64), .scale(4), .width(64)) rgb_video_1: pin names not known; wires that end beside it: CLK, DISP_REG_WRITE, rgb_video_1_p3, rgb_video_1_p4, DISP_REG_q[14:0]
  assign buffer_3_out = ALU_VALUE;  // Buffer buffer_3, 16 bits wide
  // Shift_Register #(.length(2)) shift_register_1: pin names not known; wires that end beside it: 1'b1, DISP_REG_WRITE, DISP_REG_WRITE
  Register #(.width(16)) INSTR_REG (
    .D(ALU_VALUE), .en(REG_INS_WRITE), .clk(CLK), .Q({INS_DECODER, INSTR_REG_q}));  // open: clr
  and and_5 (and_5_out[0], ~buffer_3_out[0], ~buffer_3_out[1], ~buffer_3_out[2], ~buffer_3_out[3], ~buffer_3_out[4], ~buffer_3_out[5], ~buffer_3_out[6], ~buffer_3_out[7], ~buffer_3_out[8], ~buffer_3_out[9], ~buffer_3_out[10], ~buffer_3_out[11], ~buffer_3_out[12], ~buffer_3_out[13], ~buffer_3_out[14], ~buffer_3_out[15]);  // AND_Gate
  buf buffer_4 (and_5_out[2], 1'b0);
  buf buffer_5 (and_5_out[3], 1'b0);
  buf buffer_6 (and_5_out[4], 1'b0);
  buf buffer_7 (and_5_out[5], 1'b0);
  Register register_1 (
    .D({and_5_out[7:2], CARR_BIT, and_5_out[0]}), .en(FLAG_REG_WRITE), .clk(CLK),
    .Q({register_1_q, CARRY_FLAG, ZERO_FLAG}));  // open: clr
  buf buffer_8 (and_5_out[6], 1'b0);
  buf buffer_9 (and_5_out[7], 1'b0);
  // Probe on INSTR_REG_q
  // Probe on {INS_DECODER, INSTR_REG_q}
  D_Flip_Flop d_ff_1 (.D(DISP_REG_WRITE), .clk(INV_CLK), .Q(d_ff_1_q));  // open: Qn, preset, reset
  not not_7 (not_7_out, REG_INS_WRITE);
  and and_6 (and_6_out, not_7_out, REG_INS_READ);
  assign buffer_10_out = 4'b0000;  // Buffer buffer_10, 4 bits wide
  // Probe on INS_DECODER
  Counter #(.max('h3f), .width(6)) counter_2 (
    .clk(d_ff_1_q), .carry(counter_2_carry), .Q(rgb_video_1_p3));  // open: clr, load, up, count, D
  assign ALU_VALUE = and_6_out ? {buffer_10_out, INSTR_REG_q} : 16'bz;  // Controlled_Buffer controlled_buffer_12
  Counter #(.max('h3f), .width(6)) counter_3 (
    .clk(and_7_out), .Q(rgb_video_1_p4));  // open: clr, load, up, count, D, carry
  buf and_7 (and_7_out, ~counter_2_carry);  // AND_Gate AND_Gate
  Counter #(.max('hfff), .width(12)) counter_4 (
    .clk(ROM_LOAD_CLOCK), .Q(counter_4_q));  // open: clr, load, up, count, D, carry
  Counter #(.max('h9), .width(4)) INSTR_STEP_COUNTER (
    .clr(EI), .clk(INV_CLK), .Q(INSTR_STEP_COUNTER_q));  // open: load, up, count, D, carry
  Register #(.width(16)) MEM_ADDRESS_REG (
    .D(ALU_VALUE), .en(REG_MEMADDR_WRITE), .clk(CLK), .Q(MEM_ADDRESS_REG_q));  // open: clr
  // Probe on MEM_ADDRESS_REG_q[11:0]
  // Probe on MEM_ADDRESS_REG_q
  ROM #(.addrWidth(12), .dataWidth(16)) PROGRAM_ROM (.addr(counter_4_q), .data(PROGRAM_ROM_data));
  and and_8 (and_8_out, counter_4_q[0], counter_4_q[1], counter_4_q[2], counter_4_q[3], counter_4_q[4], counter_4_q[5], counter_4_q[6], counter_4_q[7], counter_4_q[8], counter_4_q[9], counter_4_q[10], counter_4_q[11]);
  Decoder #(.enable("false"), .select(4)) decoder_1 (.sel(INSTR_STEP_COUNTER_q));  // open: out0, out1, out2, out3, out4, out5, out6, out7, out8, out9, out10, out11, out12, out13, out14, out15
  DipSwitch #(.number(10)) dipswitch_2 (
    .sw1(dipswitch_2_sw10[9]), .sw2(dipswitch_2_sw10[8]), .sw3(dipswitch_2_sw10[7]),
    .sw4(dipswitch_2_sw10[6]), .sw5(dipswitch_2_sw10[5]), .sw6(dipswitch_2_sw10[4]),
    .sw7(dipswitch_2_sw10[3]), .sw8(dipswitch_2_sw10[2]), .sw9(dipswitch_2_sw10[1]),
    .sw10(dipswitch_2_sw10[0]));
  not not_8 (not_8_out, LOAD_ROM);
  assign controlled_buffer_13_out = not_8_out ? MEM_ADDRESS_REG_q[11:0] : 12'bz;  // Controlled_Buffer controlled_buffer_13
  assign controlled_buffer_13_out = LOAD_ROM ? counter_4_q : 12'bz;  // Controlled_Buffer controlled_buffer_14
  assign controlled_buffer_15_out = not_8_out ? MEM_WRITE : 1'bz;  // Controlled_Buffer controlled_buffer_15
  assign controlled_buffer_16_out = LOAD_ROM ? ROM_LOAD_CLOCK : 1'bz;  // Controlled_Buffer controlled_buffer_16
  assign controlled_buffer_16_out = not_8_out ? CLK : 1'bz;  // Controlled_Buffer controlled_buffer_17
  not not_9 (LOAD_ROM, and_8_out);
  assign controlled_buffer_18_out = 1'b1 ? INSTR_STEP_COUNTER_q : 4'bz;  // Controlled_Buffer controlled_buffer_18
  assign controlled_buffer_19_out = 1'b1 ? {ZERO_FLAG, CARRY_FLAG} : 2'bz;  // Controlled_Buffer controlled_buffer_19
  assign controlled_buffer_20_out = 1'b1 ? INS_DECODER : 4'bz;  // Controlled_Buffer controlled_buffer_20
  not not_10 (not_10_out, 1'b1);
  assign controlled_buffer_15_out = LOAD_ROM ? LOAD_ROM : 1'bz;  // Controlled_Buffer controlled_buffer_21
  assign controlled_buffer_22_out = not_11_out ? ALU_VALUE : 16'bz;  // Controlled_Buffer controlled_buffer_22
  assign controlled_buffer_22_out = LOAD_ROM ? PROGRAM_ROM_data : 16'bz;  // Controlled_Buffer controlled_buffer_23
  not not_11 (not_11_out, LOAD_ROM);
  // Probe on {controlled_buffer_20_out, controlled_buffer_18_out, controlled_buffer_19_out}
  ROM #(.addrWidth(10), .dataWidth(14)) rom_1 (
    .addr({controlled_buffer_20_out, controlled_buffer_18_out, controlled_buffer_19_out}),
    .data({EO, COUNT_ENABLE, STOP, EI, FLAG_REG_WRITE, rom_1_data}));
  assign {controlled_buffer_20_out, controlled_buffer_18_out, controlled_buffer_19_out} = not_10_out ? dipswitch_2_sw10 : 10'bz;  // Controlled_Buffer controlled_buffer_24
  RAM #(.addrWidth(12), .asyncread("true"), .dataWidth(16), .\type ("nonvolatile")) MEMORY (
    .addr(controlled_buffer_13_out), .we(controlled_buffer_15_out), .clk(controlled_buffer_16_out),
    .din(controlled_buffer_22_out), .dout(MEMORY_dout));  // open: oe
  // Probe on {EO, COUNT_ENABLE, STOP, EI, FLAG_REG_WRITE, rom_1_data}
  // Probe on rom_1_data[8:5]
  assign ALU_VALUE = MEM_READ ? MEMORY_dout : 16'bz;  // Controlled_Buffer controlled_buffer_25
  // Probe on MEMORY_dout
  Demultiplexer #(.select(2)) demultiplexer_1 (
    .out1(SUB), .out2(MULT), .out3(DIV), .in(1'b1), .sel(rom_1_data[1:0]));  // open: out0
  Demultiplexer #(.select(3)) demultiplexer_2 (
    .out1(REG_A_READ), .out2(REG_B_READ), .out3(REG_C_READ), .out4(MEM_READ), .out5(REG_INS_READ),
    .out6(PRG_CNT_READ), .out7(EXP_READ), .in(1'b1), .sel(rom_1_data[4:2]));  // open: out0
  Demultiplexer #(.select(4)) demultiplexer_3 (
    .out1(REG_A_WRITE), .out2(REG_B_WRITE), .out3(REG_C_WRITE), .out4(REG_INS_WRITE), .out5(DISP_REG_WRITE),
    .out6(MEM_WRITE), .out7(JUMP), .out8(REG_MEMADDR_WRITE), .out9(EXP_WRITE), .in(1'b1),
    .sel(rom_1_data[8:5]));  // open: out0, out10, out11, out12, out13, out14, out15

  // Other names for the same wires on the sheet: BUS_1[15:0] = ALU_VALUE

  // Notes on the sheet:
  //   BUS VALUE
  //   DISPLAY / OUTPUT
  //   contents of PROGRAM_ROM (hex, n*v repeats v):
  //   8001 303c 703c 1064 c000 5000 8001 403c a000 8001 303d 703d 8001 3064 7064 8001 303d 703d 8000 703c
  //   84c7 4064 a019 80c8 7064 801f 403d a000 8001 3042 7042 8000 703d 8003 4042 a000 1064 4045 7064 8000
  //   7042 6000 20*0 1 0 0 0 2 0 0 20 30*0 c8 99*0 4aa 4a9 488 488 488 487 488 488 489 489 489 488 489 489
  //   489 488 488 468 488 468 889 488 4aa 489 468 67 6*467 8cb 8ca 4a9 489 488 488 489 8a9 4a9 8aa 4a9 8cb
  //   489 88a 489 8aa 8aa 489 489 468 489 68 8aa 48a 67 468 468 488 488 468 467 467 8cc 4ca 4aa 4a9 4a9
  //   4a9 4aa 8aa 4aa 8aa 8aa 8ab 8aa 8aa 8aa 4aa 4aa 8aa 489 10ec 468 488 4*489 488 889 489 468 488 468
  //   8ed 8cb 4cb 4aa 4aa 8aa 4aa 8cb 4aa 4*8cb 4ab 8aa 4aa 4aa 8aa 8ab 889 68 8aa 8aa 8ab 8aa 48a 489 489
  //   489 468 468 468 d0e 8ec 8*8cb 8ec 8cb 8cc 8ec 150e 8cb 8cb 8cc 4ab 1d70 48a 489 8ab 8ab 8ab 3616 88a
  //   469 4*489 192e d0d 5*8ec d0d 4*8ec 8ed cec 8cc d2e 1130 8cc ced cee 8cb 2e16 cee 8cc 4ab 48a 8aa 48a
  //   489 2dd3 489 489 214f 152e 110d 110e d0d 8ed d0d 8ed d0d 8ed 8ec 90e 112f 1550 112f 2592 d0f 110e
  //   8ed 8cc cee 1972 2e16 8cc 8cb 8ab 8ab 8aa 8ab 489 489 48a 2970 212f 190e 190e 150e 2dd3 110e 110e
  //   d0e 8ed cee 110f 152f 152f 192f 2192 8ed 8ed 1530 8ed 2dd4 90f d0f 8ed 8cc 8cc 8ab 48a 8ab 8aa 8aa
  //   8ab 3171 2570 214f 212f 214f 1d4f 1d2f 192f 192f 1d2f 1d2f 190f 192f 192f 1d50 110f ced d0e 2592
  //   2db3 1130 90f 8ee d0f 8ed 8cc 8cc 8cc 4*8ab 39b2 3170 2970 2970 2950 254f 2550 2550 2150 212f 2150
  //   2971 2551 2150 1d2f 1d30 1d51 39b3 2150 2d93 5afc 1130 d0f 8ee 8ee cee 8ed 8ed 8cc 8cc 8ab 8cb 3db2
  //   3991 3591 3591 3170 2d70 35b2 2970 2950 2d50 2d50 3172 41f5 3593 2550 3192 5ebb 4a37 4637 3193 29b4
  //   2193 1572 1151 90f d0f 90e 8ee 3a79 8ed 8cc 8cc 49d4 41b2 3db2 3db2 3591 3991 3571 3591 3170 3591
  //   3d92 3571 45b4 3dd4 45d4 39b3 3993 5237 39d5 35b5 2993 2172 1151 d31 d31 d2f d0f d0e 90e d0e 8ed 8ed
  //   51f5 4df4 4dd3 49d3 4192 4192 41b3 45b3 49d3 51d5 5e37 4dd5 4192 49b4 5a58 62b9 5238 45f6 41f6 39b4
  //   39d6 29b4 1d52 2e16 1171 1151 d50 d2f 90e d2f d0f d2f 5e56 5a15 51f4 51f4 4dd3 4dd4 4dd4 4dd4 6679
  //   5e37 6eba 6699 5a36 6efb 6699 669a 627a 565a 45f7 41f6 4217 39f7 2dd5 2193 21b4 1993 1171 d51 d50
  //   4ed d50 d50 6a97 6256 5e36 5a35 5a35 5614 5a15 5a15 5e36 6ed9 6698 51d5 5e57 6678 6a9a 627a 66bb
  //   5a7a 5239 4e59 4639 39f7 31f6 2dd4 2df6 1db3 1193 d92 d71 1172 d92 d92 6ef9 6ab7 6697 6676 6656 6657
  //   6677 6677 6277 72fa 72fa 66b9 6698 6efb 6aba 6aba 6adc 629a 5a7a 5259 4a39 4238 3a17 3a17 3217 29f5
  //   2e58 15b3 15b3 15b3 11b3 214c 6f1a 6ef9 6ad8 6ab7 6ab7 6ab8 6ab8 6a98 6256 6a98 72fb 6297 775c 6ada
  //   6efb 190b 14ca 66db 5e9b 5a7a 4e79 4e7a 4259 469a 3a38 3237 2a16 2616 21f5 2216 2636 2d8f 775b 731a
  //   6f19 6ef9 6ef9 6ef9 6f1a 6f1a 6f1a 6ad8 6ad9 777d 6afa 6ada 190b 8a8 150b 62db 5ebb 5a9a 569a 4e99
  //   4679 4a9a 3e79 3a78 3658 3678 2e36 3257 298f 190b 777b 775b 773a 733a 733a 6f3a 733a 6af9 6af9 6af9
  //   14e9 150b 190b 192c 24 150b 150b 14eb 62db 5eda 216e 258f 887 56fc 4aba 4299 3e79 3a99 3a98 3e99
  //   2db0 31b0 777c 775b 775b 735b 10e9 6f3a 733a 6f1a 1cea ce9 150b 150b 192c 150b 192c 1d4d 192c 192c
  //   150b 298f 1d4d 190a 1d4d 152b 56fb 4eda 4aba 46da 3a98 214d 216e 256e 7b9d 777c 777c 214d 150a 10ea
  //   10ea 192c 150b 192b 150b 1d2c 214e 298f 1d4d 1d4c 192c 35f2 216e 1d4d 214e 23 44 150b 150b 152b 52fa
  //   4eda 44 256f 256e 256f 779d 777c 1d4c 214d 214d 10ea 192c 256f 192c 1d4d 258f 190a 29b0 1d2c 444 443
  //   216e 1d4e 258f 298f 258f 10c8 150b 1d4d 192c 192d 192c 152c 216e 466 256f 29b0 779d 10e9 64 1d2c
  //   192b 298f 192c 216e 65 23 44 23 44 44 444 444 23 150b 1d6d cc8 23 44 1d4d 192c 216e 258f 43 44 43 23
  //   44 65 192c 1d4d 2990 256e 35d1 258f 22 43 43 44 44 444 44 4*43 23 216e ca7 887 31d1 258f 44 444 44
  //   443 444 443 465 44 43 216e 31d1 1d4d 29b0 464 444 43 23 465 43 443 44 44 444 44 44 43 464 44 ca7
  //   31d1 43 43 443 444 44 44 44 465 465 43 444 465 43 464 44 465 43 23 43 885 43 44 43 464 486 ca7 44 43
  //   464 443 444 43 23 43 64 444 486 486 464 64 444 65 444 43 43 465 465 44 43 444 464 43 43 423 65 44
  //   485 43 465 44 485 44 23 444 485 44 43 486 65 43 443 43 443 43 44 444 43 465 466 43 443 443 444 43
  //   444 465 464 465 465 44 43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
  //   contents of rom_1 (hex, n*v repeats v):
  //   4*118 4*1090 4*400 52*0 4*118 4*1090 4*100 4*20 4*400 44*0 4*118 4*1090 4*100 4*40 4*400 44*0 4*118
  //   4*1090 4*100 4*40 4*2220 4*400 40*0 4*118 4*1090 4*100 4*40 4*2220 4*400 40*0 4*118 4*1090 4*a0
  //   4*400 48*0 4*118 4*1090 4*e0 4*400 48*0 4*118 4*1090 4*100 4*c0 4*400 44*0 4*118 4*1090 4*20 4*400
  //   48*0 4*118 4*1090 400 400 e0 e0 4*400 48*0 4*118 4*1090 400 e0 400 e0 4*400 48*0 4*118 4*1090 4*800
  //   4*400 48*0 4*118 4*1090 4*100 4*20 4*400
endmodule
